# Fritzing sketch grbl interface board V3 (saved by Fritzing 0.9.3b)
circuit board: 4.1275cm x 6.35cm
breadboards: 1

parts:
  C3 = Ceramic Capacitor [capacitance=0.1µF voltage=50V package="100 mil [THT, multilayer]"]
  C4 = Ceramic Capacitor [capacitance=0.1µF voltage=50V package="100 mil [THT, multilayer]"]
  J1 = DB25 - 26pin Header [part_number=70246-2601 form="♂ (shrouded male)" package=THT]
  J2 = screw terminal, 2 pins [part_number=PRT-08084]
  J3 = screw terminal, 2 pins [part_number=PRT-08084]
  J4 = screw terminal, 2 pins [part_number=PRT-08084]
  C5 = Ceramic Capacitor [capacitance=0.1µF voltage=50V package="100 mil [THT, multilayer]"]
  C6 = Ceramic Capacitor [capacitance=0.1µF voltage=50V package="100 mil [THT, multilayer]"]
  C7 = Ceramic Capacitor [capacitance=0.1µF voltage=50V package="100 mil [THT, multilayer]"]
  Part1 = Arduino Nano (Rev3.0)
  C2 = Ceramic Capacitor [capacitance=0.1µF voltage=50V package="100 mil [THT, multilayer]"]

nets:
  gnd: C3.0, C4.0, J1.pin25, J1.pin24, J1.pin23, J1.pin22, J1.pin21, J1.pin20, J1.pin19, J1.pin18, J2.pin2, J3.pin2, J4.pin2, C5.1, C6.1, C7.1, Part1.GND, C2.0
  D9: C3.1, J1.pin10, Part1.D9
  D10: C4.1, J1.pin11, Part1.D10
  D13: J1.pin1, Part1.D13/SCK
  D2: J1.pin2, Part1.D2
  D5: J1.pin3, Part1.D5
  D3: J1.pin4, J1.pin8, Part1.D3
  D6: J1.pin5, J1.pin9, Part1.D6
  D4: J1.pin6, Part1.D4
  D7: J1.pin7, Part1.D7
  D12: J1.pin12, Part1.D12/MISO, C2.1
  A5: J1.pin13, Part1.A5
  A3: J1.pin17, Part1.A3
  D11: J1.pin14, Part1.D11/MOSI
  N1: J2.pin1, C7.0, Part1.A0
  N2: J3.pin1, C6.0, Part1.A1
  N3: J4.pin1, C5.0, Part1.A2

notes:
  USB
  104
  G540 Interface board
  V3
  Monson 10/8/2016
  Feed/Hold
  Reset/Abort
  Start/Resume
  gnd
  A0
  A1
  A2
  Contact@509maker.com

custom parts:
  DB25 - 26pin Header: 26pin Header for use with parallel port 26-pin female header to DB25 female/male cable.
